# Fritzing sketch desktop-box (saved by Fritzing 0.9.3b)
circuit board: 5.26219cm x 6.39036cm
breadboards: 1

parts:
  J3 = double row female pin header, 40 pins [form="♀ (female)"]
  J2 = double row female pin header, 24 pins [form="♀ (female)"]
  J1 = double row female pin header, 24 pins [form="♀ (female)"]
  R1 = Resistor [tolerance=±5% resistance=220 package=THT]
  R2 = Resistor [tolerance=±5% resistance=220 package=THT]
  R3 = Resistor [tolerance=±5% resistance=220 package=THT]
  R4 = Resistor [tolerance=±5% resistance=220 package=THT]
  R5 = Resistor [tolerance=±5% resistance=220 package=THT]
  R6 = Resistor [tolerance=±5% resistance=220 package=THT]
  R7 = Resistor [tolerance=±5% resistance=220 package=THT]
  R8 = Resistor [tolerance=±5% resistance=220 package=THT]
  R9 = Resistor [tolerance=±5% resistance=220 package=THT]
  U1 = Darlington Driver [package=so18l]
  ULN2 = Darlington Driver [package=so18l]
  R10 = Resistor [tolerance=±5% resistance=220 package=THT]
  R11 = Resistor [tolerance=±5% resistance=220 package=THT]
  R12 = Resistor [tolerance=±5% resistance=220 package=THT]
  R13 = Resistor [tolerance=±5% resistance=220 package=THT]
  R14 = Resistor [tolerance=±5% resistance=220 package=THT]
  R15 = Resistor [tolerance=±5% resistance=220 package=THT]
  R16 = Resistor [tolerance=±5% resistance=220 package=THT]
  R17 = Resistor [tolerance=±5% resistance=220 package=THT]
  R18 = Resistor [tolerance=±5% resistance=220 package=THT]
  R19 = Resistor [tolerance=±5% resistance=220 package=THT]
  R20 = Resistor [tolerance=±5% resistance=220 package=THT]
  R21 = Resistor [tolerance=±5% resistance=220 package=THT]
  R22 = Resistor [tolerance=±5% resistance=220 package=THT]
  R23 = Resistor [tolerance=±5% resistance=220 package=THT]
  R24 = Resistor [tolerance=±5% resistance=220 package=THT]
  ULN3 = Darlington Driver [package=so18l]
  5V_3V3_GND = male pin header, 3 pins [form="♂ (male)"]
  J5 = double row male pin header, 8 pins [form="♂ (male)"]

nets:
  N1: J3.pin1, 5V_3V3_GND.pin2
  N2: J3.pin2, U1.7
  N3: J3.pin3, U1.6
  N4: J3.pin4, U1.5
  N5: J3.pin6, U1.4
  N6: J3.pin7, U1.3
  N7: J3.pin8, U1.2
  N8: J3.pin10, U1.1
  N9: J3.pin11, J5.pin8
  N10: J3.pin12, J5.pin7
  N11: J3.pin14, J5.pin6
  N12: J3.pin15, J5.pin5
  N13: J3.pin16, ULN2.8
  N14: J3.pin17, ULN2.7
  N15: J3.pin18, ULN2.6
  N16: J3.pin19, ULN2.5
  N17: J3.pin21, ULN2.4
  N18: J3.pin22, ULN2.3
  N19: J3.pin23, ULN2.2
  N20: J3.pin25, ULN2.1
  N21: J3.pin27, ULN3.8
  N22: J3.pin28, ULN3.7
  N23: J3.pin29, ULN3.6
  N24: J3.pin30, ULN3.5
  N25: J3.pin31, J3.pin38, U1.9, ULN2.9, ULN3.9, 5V_3V3_GND.pin3, J5.pin1, J5.pin2, J5.pin3, J5.pin4
  N26: J3.pin32, ULN3.4
  N27: J3.pin33, ULN3.3
  N28: J3.pin35, ULN3.2
  N29: J3.pin36, ULN3.1
  N30: J3.pin37, U1.8
  N31: J3.pin39, J3.pin40, J2.pin13, J2.pin14, J2.pin15, J2.pin16, J2.pin17, J2.pin18, J2.pin19, J2.pin20, J2.pin21, J2.pin22, J2.pin23, J2.pin24, J1.pin13, J1.pin14, J1.pin15, J1.pin16, J1.pin17, J1.pin18, J1.pin19, J1.pin20, J1.pin21, J1.pin22, J1.pin23, J1.pin24, 5V_3V3_GND.pin1
  N32: J2.pin1, R13.Pin_1
  N33: J2.pin2, R14.Pin_1
  N34: J2.pin3, R15.Pin_1
  N35: J2.pin4, R16.Pin_1
  N36: J2.pin5, R17.Pin_1
  N37: J2.pin6, R18.Pin_1
  N38: J2.pin7, R19.Pin_1
  N39: J2.pin8, R20.Pin_1
  N40: J2.pin9, R21.Pin_1
  N41: J2.pin10, R22.Pin_1
  N42: J2.pin11, R23.Pin_1
  N43: J2.pin12, R24.Pin_1
  N44: J1.pin1, R1.Pin_1
  N45: J1.pin2, R2.Pin_1
  N46: J1.pin3, R3.Pin_1
  N47: J1.pin4, R4.Pin_1
  N48: J1.pin5, R5.Pin_1
  N49: J1.pin6, R6.Pin_1
  N50: J1.pin7, R7.Pin_1
  N51: J1.pin8, R8.Pin_1
  N52: J1.pin9, R9.Pin_1
  N53: J1.pin10, R10.Pin_1
  N54: J1.pin11, R11.Pin_1
  N55: J1.pin12, R12.Pin_1
  N56: R1.Pin_0, U1.18
  N57: R2.Pin_0, U1.17
  N58: R3.Pin_0, U1.16
  N59: R4.Pin_0, U1.15
  N60: R5.Pin_0, U1.14
  N61: R6.Pin_0, U1.13
  N62: R7.Pin_0, U1.12
  N63: R8.Pin_0, U1.11
  N64: R9.Pin_0, ULN3.18
  N65: ULN2.11, R24.Pin_0
  N66: ULN2.12, R23.Pin_0
  N67: ULN2.13, R22.Pin_0
  N68: ULN2.14, R21.Pin_0
  N69: ULN2.15, R20.Pin_0
  N70: ULN2.16, R19.Pin_0
  N71: ULN2.17, R18.Pin_0
  N72: ULN2.18, R17.Pin_0
  N73: R10.Pin_0, ULN3.17
  N74: R11.Pin_0, ULN3.16
  N75: R12.Pin_0, ULN3.15
  N76: R13.Pin_0, ULN3.14
  N77: R14.Pin_0, ULN3.13
  N78: R15.Pin_0, ULN3.12
  N79: R16.Pin_0, ULN3.11

notes:
  RPi GPIO
  1  2
  39 40
  GPIO: 5  0  11 9
  GND
  ULN2803
