# Fritzing sketch meeting-room-info (saved by Fritzing 0.9.3b)
circuit board: 4.22037cm x 5.84384cm
breadboards: 1

parts:
  Buttons = double row female pin header, 6 pins [form="♀ (female)"]
  Contrast = mystery part, 3 pins [chip_label=?]
  Backlight = mystery part, 3 pins [chip_label=?]
  R1 = Resistor [tolerance=±5% resistance=220 package=THT]
  RPi = mystery part, 40 pins [chip_label=?]
  LCD = mystery part, 18 pins [chip_label=?]
  R2 = Resistor [tolerance=±5% resistance=220 package=THT]
  Q1 = NPN-Transistor [package="TO92 [THT]"]
  Q2 = NPN-Transistor [package="TO92 [THT]"]
  R3 = Resistor [tolerance=±5% resistance=220 package=THT]
  R4 = Resistor [tolerance=±5% resistance=220 package=THT]
  Output = double row female pin header, 4 pins [form="♀ (female)"]

nets:
  N1: Buttons.pin1, RPi.pin28
  N2: Buttons.pin2, RPi.pin25
  N3: Buttons.pin3, RPi.pin23
  N4: Buttons.pin4, Buttons.pin5, Buttons.pin6, Contrast.pin3, RPi.pin34, LCD.pin7, LCD.pin10, Q1.E, Q2.E
  N5: Contrast.pin1, Backlight.pin1, RPi.pin39, RPi.pin40, Output.pin3, Output.pin4
  N6: Contrast.pin2, LCD.pin13
  N7: Backlight.pin2, LCD.pin9
  N8: R1.Pin_0, Q1.C
  N9: R1.Pin_1, Output.pin2
  N10: RPi.pin2, LCD.pin18
  N11: RPi.pin3, LCD.pin17
  N12: RPi.pin4, LCD.pin16
  N13: RPi.pin6, LCD.pin15
  N14: RPi.pin21, R4.Pin_0
  N15: RPi.pin22, R3.Pin_0
  N16: RPi.pin29, LCD.pin8
  N17: RPi.pin30, LCD.pin6
  N18: RPi.pin32, LCD.pin5
  N19: RPi.pin33, LCD.pin4
  N20: RPi.pin35, LCD.pin3
  N21: RPi.pin36, LCD.pin2
  N22: RPi.pin37, LCD.pin1
  N23: R2.Pin_0, Q2.C
  N24: R2.Pin_1, Output.pin1
  N25: Q1.B, R3.Pin_1
  N26: Q2.B, R4.Pin_1
