# Fritzing sketch traffic-light-controller (saved by Fritzing 0.9.3b)
circuit board: 14.388cm x 15.347cm

parts:
  IC1 = ULN2803A [part_number=ULN2803A package=THT]
  U1 = Sharp PC847X [part_number=TLP521-4 package=THT]
  R1 = Resistor [tolerance=±5% resistance=100 package=THT]
  R2 = Resistor [tolerance=±5% resistance=100 package=THT]
  R8 = Resistor [tolerance=±5% resistance=100 package=THT]
  R7 = Resistor [tolerance=±5% resistance=100 package=THT]
  R6 = Resistor [tolerance=±5% resistance=100 package=THT]
  R5 = Resistor [tolerance=±5% resistance=100 package=THT]
  R4 = Resistor [tolerance=±5% resistance=100 package=THT]
  R3 = Resistor [tolerance=±5% resistance=100 package=THT]
  U2 = Sharp PC847X [part_number=TLP521-4 package=THT]
  J6 = Camdenboss CTB0158-12 [part_number=CTB0158-12 package=THT]
  J5 = Camdenboss CTB0158-2 [part_number=CTB0158-2 package=THT]
  J7 = Camdenboss CTB0158-12 [part_number=CTB0158-12 package=THT]
  J10 = shrouded pin header, 40 pins [form="♂ (shrouded male)"]
  LED1 = LED - 5mm [color="Green (555nm)" package="5 mm [THT]"]
  LED2 = LED - 5mm [color="Red (633nm)" package="5 mm [THT]"]
  LED3 = LED - 5mm [color="Green (555nm)" package="5 mm [THT]"]
  LED4 = LED - 5mm [color="Red (633nm)" package="5 mm [THT]"]
  LED5 = LED - 5mm [color="Green (555nm)" package="5 mm [THT]"]
  LED6 = LED - 5mm [color="Red (633nm)" package="5 mm [THT]"]
  LED7 = LED - 5mm [color="Green (555nm)" package="5 mm [THT]"]
  LED8 = LED - 5mm [color="Red (633nm)" package="5 mm [THT]"]
  J3 = Camdenboss CTB0158-2 [part_number=CTB0158-2 package=THT]
  12V_C+ = Power plug
  LED9 = LED - 5mm [color="Green (555nm)" package="5 mm [THT]"]
  LED10 = LED - 5mm [color="Green (555nm)" package="5 mm [THT]"]
  LED11 = LED - 5mm [color="Green (555nm)" package="5 mm [THT]"]
  LED12 = LED - 5mm [color="Green (555nm)" package="5 mm [THT]"]
  LED13 = LED - 5mm [color="Red (633nm)" package="5 mm [THT]"]
  LED14 = LED - 5mm [color="Red (633nm)" package="5 mm [THT]"]
  LED15 = LED - 5mm [color="Red (633nm)" package="5 mm [THT]"]
  LED16 = LED - 5mm [color="Red (633nm)" package="5 mm [THT]"]
  IC2 = ULN2803A [part_number=ULN2803A package=THT]
  U3 = Sharp PC847X [part_number=TLP521-4 package=THT]
  U4 = Sharp PC847X [part_number=TLP521-4 package=THT]
  R9 = Resistor [tolerance=±5% resistance=100 package=THT]
  R10 = Resistor [tolerance=±5% resistance=100 package=THT]
  R11 = Resistor [tolerance=±5% resistance=100 package=THT]
  R12 = Resistor [tolerance=±5% resistance=100 package=THT]
  R13 = Resistor [tolerance=±5% resistance=100 package=THT]
  R14 = Resistor [tolerance=±5% resistance=100 package=THT]
  R15 = Resistor [tolerance=±5% resistance=100 package=THT]
  R16 = Resistor [tolerance=±5% resistance=100 package=THT]
  LED17 = LED - 5mm [color="Green (555nm)" package="5 mm [THT]"]
  LED18 = LED - 5mm [color="Green (555nm)" package="5 mm [THT]"]
  LED19 = LED - 5mm [color="Green (555nm)" package="5 mm [THT]"]
  LED20 = LED - 5mm [color="Green (555nm)" package="5 mm [THT]"]
  LED21 = LED - 5mm [color="Red (633nm)" package="5 mm [THT]"]
  LED22 = LED - 5mm [color="Red (633nm)" package="5 mm [THT]"]
  LED23 = LED - 5mm [color="Red (633nm)" package="5 mm [THT]"]
  LED24 = LED - 5mm [color="Red (633nm)" package="5 mm [THT]"]
  IC3 = ULN2803A [part_number=ULN2803A package=THT]
  U5 = Sharp PC847X [part_number=TLP521-4 package=THT]
  U6 = Sharp PC847X [part_number=TLP521-4 package=THT]
  R17 = Resistor [tolerance=±5% resistance=100 package=THT]
  R18 = Resistor [tolerance=±5% resistance=100 package=THT]
  R19 = Resistor [tolerance=±5% resistance=100 package=THT]
  R20 = Resistor [tolerance=±5% resistance=100 package=THT]
  R21 = Resistor [tolerance=±5% resistance=100 package=THT]
  R22 = Resistor [tolerance=±5% resistance=100 package=THT]
  R23 = Resistor [tolerance=±5% resistance=100 package=THT]
  R24 = Resistor [tolerance=±5% resistance=100 package=THT]
  J11 = Camdenboss CTB0158-12 [part_number=CTB0158-12 package=THT]
  J12 = Camdenboss CTB0158-12 [part_number=CTB0158-12 package=THT]
  Q1 = NPN-Transistor [part_number=BC547B package="TO92 [THT]"]
  U7 = mystery part, 3 pins [chip_label="Buzzer 400Hz"]
  R25 = Resistor [tolerance=±5% resistance=10k package=THT]
  Q2 = NPN-Transistor [part_number=BC547B package="TO92 [THT]"]
  U8 = mystery part, 3 pins [chip_label="Buzzer 2300Hz"]
  R26 = Resistor [tolerance=±5% resistance=10k package=THT]

nets:
  N1: IC1.In_1, J10.pin7
  N2: IC1.In_2, J10.pin6
  N3: IC1.In_3, J10.pin4
  N4: IC1.In_4, J10.pin3
  N5: IC1.In_5, J10.pin2
  N6: IC1.In_6, J10.pin37
  N7: IC1.In_7, J10.pin36
  N8: IC1.In_8, J10.pin35
  0V: IC1.0V, J10.pin5, J10.pin13, J10.pin20, J3.pin2, IC2.0V, IC3.0V, Q1.E, Q2.E
  N9: IC1.Out_8, R8.Pin_0
  N10: IC1.Out_7, R7.Pin_0
  N11: IC1.Out_6, R6.Pin_0
  N12: IC1.Out_5, R5.Pin_0
  N13: IC1.Out_4, R4.Pin_0
  N14: IC1.Out_3, R3.Pin_0
  N15: IC1.Out_2, R2.Pin_0
  N16: IC1.Out_1, R1.Pin_0
  5V: U1.Pin_1, U1.Pin_3, U1.Pin_5, U1.Pin_7, U2.Pin_1, U2.Pin_3, U2.Pin_5, U2.Pin_7, J10.pin39, J10.pin40, J3.pin1, U3.Pin_1, U3.Pin_3, U3.Pin_5, U3.Pin_7, U4.Pin_1, U4.Pin_3, U4.Pin_5, U4.Pin_7, U5.Pin_1, U5.Pin_3, U5.Pin_5, U5.Pin_7, U6.Pin_1, U6.Pin_3, U6.Pin_5, U6.Pin_7, U7.pin1, U8.pin1
  N17: U1.Pin_2, LED1.anode
  N18: U1.Pin_4, LED2.anode
  N19: U1.Pin_6, LED3.anode
  N20: U1.Pin_8, LED4.anode
  0.12V: U1.Pin_9, U1.Pin_11, U1.Pin_13, U1.Pin_15, U2.Pin_9, U2.Pin_11, U2.Pin_13, U2.Pin_15, J5.pin2, 12V_C+.GND, U3.Pin_9, U3.Pin_11, U3.Pin_13, U3.Pin_15, U4.Pin_9, U4.Pin_11, U4.Pin_13, U4.Pin_15, U5.Pin_9, U5.Pin_11, U5.Pin_13, U5.Pin_15, U6.Pin_9, U6.Pin_11, U6.Pin_13, U6.Pin_15
  N21: U1.Pin_10, J6.pin4
  N22: U1.Pin_12, J6.pin3
  N23: U1.Pin_14, J6.pin2
  N24: U1.Pin_16, J6.pin1
  N25: R1.Pin_1, LED1.cathode
  N26: R2.Pin_1, LED2.cathode
  N27: R8.Pin_1, LED8.cathode
  N28: R7.Pin_1, LED7.cathode
  N29: R6.Pin_1, LED6.cathode
  N30: R5.Pin_1, LED5.cathode
  N31: R4.Pin_1, LED4.cathode
  N32: R3.Pin_1, LED3.cathode
  N33: U2.Pin_2, LED5.anode
  N34: U2.Pin_4, LED6.anode
  N35: U2.Pin_6, LED7.anode
  N36: U2.Pin_8, LED8.anode
  N37: U2.Pin_10, J6.pin8
  N38: U2.Pin_12, J6.pin7
  N39: U2.Pin_14, J6.pin6
  N40: U2.Pin_16, J6.pin5
  N41: J6.pin9, U4.Pin_16
  N42: J6.pin10, U4.Pin_14
  N43: J6.pin11, U4.Pin_12
  N44: J6.pin12, U4.Pin_10
  12V: J5.pin1, J7.pin1, J7.pin2, J7.pin3, J7.pin4, J7.pin5, J7.pin6, J7.pin7, J7.pin8, J7.pin9, J7.pin10, J7.pin11, J7.pin12, 12V_C+.VCC, J12.pin1, J12.pin2, J12.pin3, J12.pin4, J12.pin5, J12.pin6, J12.pin7, J12.pin8, J12.pin9, J12.pin10, J12.pin11, J12.pin12
  N45: J10.pin14, IC3.In_8
  N46: J10.pin15, IC3.In_7
  N47: J10.pin16, IC3.In_6
  N48: J10.pin17, IC3.In_5
  N49: J10.pin18, IC3.In_4
  N50: J10.pin19, IC3.In_3
  N51: J10.pin21, IC3.In_2
  N52: J10.pin22, IC3.In_1
  N53: J10.pin23, IC2.In_8
  N54: J10.pin25, IC2.In_7
  N55: J10.pin27, IC2.In_6
  N56: J10.pin28, IC2.In_5
  N57: J10.pin29, IC2.In_4
  N58: J10.pin30, IC2.In_3
  N59: J10.pin32, IC2.In_2
  N60: J10.pin33, IC2.In_1
  N61: LED9.cathode, R13.Pin_1
  N62: LED9.anode, U3.Pin_6
  N63: LED10.cathode, R11.Pin_1
  N64: LED10.anode, U3.Pin_2
  N65: LED11.cathode, R9.Pin_1
  N66: LED11.anode, U4.Pin_6
  N67: LED12.cathode, R16.Pin_1
  N68: LED12.anode, U4.Pin_2
  N69: LED13.cathode, R14.Pin_1
  N70: LED13.anode, U3.Pin_8
  N71: LED14.cathode, R12.Pin_1
  N72: LED14.anode, U3.Pin_4
  N73: LED15.cathode, R10.Pin_1
  N74: LED15.anode, U4.Pin_8
  N75: LED16.cathode, R15.Pin_1
  N76: LED16.anode, U4.Pin_4
  N77: IC2.Out_8, R14.Pin_0
  N78: IC2.Out_7, R13.Pin_0
  N79: IC2.Out_6, R12.Pin_0
  N80: IC2.Out_5, R11.Pin_0
  N81: IC2.Out_4, R10.Pin_0
  N82: IC2.Out_3, R9.Pin_0
  N83: IC2.Out_2, R15.Pin_0
  N84: IC2.Out_1, R16.Pin_0
  N85: U3.Pin_10, J11.pin4
  N86: U3.Pin_12, J11.pin3
  N87: U3.Pin_14, J11.pin2
  N88: U3.Pin_16, J11.pin1
  N89: LED17.cathode, R21.Pin_1
  N90: LED17.anode, U5.Pin_6
  N91: LED18.cathode, R19.Pin_1
  N92: LED18.anode, U5.Pin_2
  N93: LED19.cathode, R17.Pin_1
  N94: LED19.anode, U6.Pin_6
  N95: LED20.cathode, R24.Pin_1
  N96: LED20.anode, U6.Pin_2
  N97: LED21.cathode, R22.Pin_1
  N98: LED21.anode, U5.Pin_8
  N99: LED22.cathode, R20.Pin_1
  N100: LED22.anode, U5.Pin_4
  N101: LED23.cathode, R18.Pin_1
  N102: LED23.anode, U6.Pin_8
  N103: LED24.cathode, R23.Pin_1
  N104: LED24.anode, U6.Pin_4
  N105: IC3.Out_8, R22.Pin_0
  N106: IC3.Out_7, R21.Pin_0
  N107: IC3.Out_6, R20.Pin_0
  N108: IC3.Out_5, R19.Pin_0
  N109: IC3.Out_4, R18.Pin_0
  N110: IC3.Out_3, R17.Pin_0
  N111: IC3.Out_2, R23.Pin_0
  N112: IC3.Out_1, R24.Pin_0
  N113: U5.Pin_10, J11.pin12
  N114: U5.Pin_12, J11.pin11
  N115: U5.Pin_14, J11.pin10
  N116: U5.Pin_16, J11.pin9
  N117: U6.Pin_10, J11.pin8
  N118: U6.Pin_12, J11.pin7
  N119: U6.Pin_14, J11.pin6
  N120: U6.Pin_16, J11.pin5
  N121: Q1.B, R25.Pin_1
  N122: Q1.C, U7.pin3
  N123: Q2.B, R26.Pin_1
  N124: Q2.C, U8.pin3

notes:
  0V
  12V
  5V
  Lamps
  RPi GPIO
  Granta
  Traffic
  Lights
  Note that header pinouts are labelled differently from jumper socket pinouts.
  See gpio pinout.txt for mapping between the two
